# Fritzing sketch p1reader-board (saved by Fritzing 0.9.3b)

parts:
  Part1 = iotsa esp-12 experiment board
  R1 = Resistor [tolerance=±5% resistance=470 package=THT]  # not connected

nets:
  N1: Part1.pin_15, Part1.pin_110, Part1.pin_111
  N2: Part1.pin_16, Part1.pin_89, Part1.pin_90, Part1.pin_91, Part1.pin_119, Part1.pin_120
  N3: Part1.pin_40, Part1.pin_117, Part1.pin_118

notes:
  RJ11 p1 - 5V Power (nc)
  RJ11 p2 - Request (IO13 pullup)
  RJ11 p3 - Data GND
  RJ11 p4 - nc
  RJ11 p5 - Data (IO12)
  RJ11 p6 - Power GND (nc)

custom parts:
  iotsa esp-12 experiment board: Board with an ESP-12, a power supply, reset button, FTDI plug and experiment area.
